# Fritzing sketch Untitled Sketch (saved by Fritzing 0.9.4)
breadboards: 1

parts:
  D2 = Rectifier Diode [part_number=0 package="300 mil [THT]"]
  D3 = Rectifier Diode [part_number=1N4001 package="300 mil [THT]"]
  D4 = Rectifier Diode [part_number=1N4001 package="300 mil [THT]"]
  C1 = Ceramic Capacitor [capacitance="100 nF" package="0603 [SMD, multilayer]"]
  U3 = MLX90614 [package=to-39]
  Power_plug1 = Power plug
  R1 = Resistor [tolerance=±5% resistance=220 package="1206 [SMD]"]
  R2 = Resistor [tolerance=±5% resistance=220 package="1206 [SMD]"]
  R3 = Resistor [tolerance=±5% resistance=220 package="1206 [SMD]"]
  R4 = Resistor [tolerance=±5% resistance=220 package="1206 [SMD]"]
  R5 = Resistor [tolerance=±5% resistance=220 package="1206 [SMD]"]
  R6 = Resistor [tolerance=±5% resistance=220 package="1206 [SMD]"]
  5V = Diode [package=diode-hv]  # not connected
  U6 = Transformer [package=transformer]
  D1 = Rectifier Diode [part_number=1N4001 package="300 mil [THT]"]
  Model_LM358P = OP482 - Low Power, High Speed JFET Quad Operational Amplifier [part_number=OP482]

nets:
  N1: D2.cathode, U6.3, D1.anode
  N2: D2.anode, D4.anode, C1.0, U3.PWM_SDA, Model_LM358P.V+
  N3: D3.cathode, C1.1, U3.SCL_VZ, D1.cathode
  N4: D3.anode, D4.cathode, U6.4
  N5: U3.VDD, R1.Pin_1, R2.Pin_0, R5.Pin_0
  VSS: U3.VSS, Power_plug1.GND
  N6: Power_plug1.VCC, R1.Pin_0, R3.Pin_0
  N7: R2.Pin_1, Model_LM358P.+IND
  N8: R3.Pin_1, R4.Pin_0, Model_LM358P.-IND
  N9: R4.Pin_1, Model_LM358P.OUTD
  N10: R5.Pin_1, R6.Pin_0
  GND: R6.Pin_1
